# Fritzing sketch 1602_LCD (saved by Fritzing 0.9.2b)
breadboards: 1

parts:
  R1 = Rotary Potentiometer (Small) [maximum_resistance=5kΩ package=THT]
  Arduino1 = Arduino Uno (Rev3)
  LCD1 = LCD screen
  R2 = Resistor [tolerance=±5% resistance=100 package=THT]

nets:
  GND: R1.leg1, Arduino1.GND, LCD1.VSS, LCD1.LED-
  N1: R1.wiper, LCD1.V0
  5V: R1.leg2, Arduino1.5V, LCD1.VDD
  N2: Arduino1.D10_PWM/SS, LCD1.E
  N3: Arduino1.D11_PWM/MOSI, LCD1.R/W
  N4: Arduino1.D12/MISO, LCD1.RS
  N5: Arduino1.D13/SCK, R2.Pin_0
  N6: Arduino1.D2, LCD1.DB7
  N7: Arduino1.D3_PWM, LCD1.DB6
  N8: Arduino1.D4, LCD1.DB5
  N9: Arduino1.D5_PWM, LCD1.DB4
  N10: LCD1.LED+, R2.Pin_1

notes:
  LCD Pin
  Connect to
  1 (VSS)
  GND Arduino pin*
  2 (VDD)
  + 5v Arduino pin
  3 (contrast)
  5 K otentiometer to GND Arduino pin
  4 RS
  Arduino pin 12
  5 R/W
  Arduino pin 11
  6 Enable
  Arduino pin 10
  11 (Data 4)
  Arduino pin 5
  12 (Data 5)
  Arduino pin 4
  13 (Data 6)
  Arduino pin 3
  14 (Data 7)
  Arduino pin 2
  15 Backlight +
  100 R to Arduino pin 13
  16 Backlight GND
  GND Arduino pin

// code stored in the sketch: LCD.ino
#include <LiquidCrystal.h>

LiquidCrystal lcd(12,11,10,5,4,3,2);
int back=13;

void setup() {
pinMode(back, OUTPUT);
digitalWrite(back, HIGH);
lcd.begin(16,2);
}

void loop() {
lcd.setCursor(0,0);
lcd.print("Hello YouTube");
lcd.setCursor(0,1);
lcd.print(millis()/1000);
}
